// Logisim project Hussein_Kazem_5667 Digital Clock Simulator.circ as structural Verilog: 11 circuits, main circuit main
module main (
);

  wire A_P, AH, ah_t, BH, bh_t, C, CH, ch_t, DH, dh_t, EH, eh_t, FH, fh_t, GH, gh_t, H, M, m_t, S, s_t;
  wire [3:0] MI, mi_t, SI, si_t;

  Button u_A_P (.out(A_P));
  _7_Segment_Display u_7_segment_display_1 (.g(1'b1), .f(1'b1), .a(1'b1), .b(1'b1), .e(1'b1), .c(C));  // open: d, dp
  _7_Segment_Display u_7_segment_display_2 (.g(GH), .f(FH), .a(AH), .b(BH), .e(EH), .d(DH), .c(CH));  // open: dp
  Button u_H (.out(H));
  _7_Segment_Display u_7_segment_display_3 (
    .g(gh_t), .f(fh_t), .a(ah_t), .b(bh_t), .e(eh_t), .d(dh_t), .c(ch_t));  // open: dp
  Clock clock_1 (
    .H_2({GH, FH, EH, DH, CH, BH, AH}), .h_3({gh_t, fh_t, eh_t, dh_t, ch_t, bh_t, ah_t}), .M_3(MI),
    .m_4(mi_t), .S_3(SI), .s_4(si_t), .C_A_P(C), .S_2(S), .M_2(M), .s(s_t), .m(m_t), .H(H), .A_P(A_P));
  Button u_M (.out(M));
  Hex_Digit_Display hex_digit_display_1 (.value(MI));  // open: dp
  Button m_2 (.out(m_t));
  Hex_Digit_Display hex_digit_display_2 (.value(mi_t));  // open: dp
  Button u_S (.out(S));
  Button s_2 (.out(s_t));
  Hex_Digit_Display hex_digit_display_3 (.value(si_t));  // open: dp
  Hex_Digit_Display hex_digit_display_4 (.value(SI));  // open: dp
endmodule

module _7_segment_decoder (
  input  [3:0] in_1,
  output a,
  output b,
  output c,
  output d,
  output e,
  output f,
  output g
);

  wire and_1_out, and_2_out, and_3_out, and_4_out, and_5_out, and_6_out, and_7_out, and_8_out, and_9_out,
       and_10_out, and_11_out, and_12_out, and_13_out, and_14_out, and_15_out, and_16_out, and_17_out,
       and_18_out, and_19_out, and_20_out, and_21_out, and_22_out, and_23_out, and_24_out, and_25_out,
       and_26_out, and_27_out, and_28_out, and_29_out, not_1_out, not_2_out, not_3_out, not_4_out, not_5_out,
       not_6_out, not_7_out, not_8_out, not_9_out, not_10_out, not_11_out, not_12_out, not_13_out,
       not_14_out, not_15_out, not_16_out, not_17_out, not_18_out, not_19_out, not_20_out, not_21_out,
       not_22_out, not_23_out, not_24_out, not_25_out, not_26_out, not_27_out, not_28_out, not_29_out,
       not_30_out, not_31_out, not_32_out, not_33_out, not_34_out, not_35_out, not_36_out;

  not not_1 (not_1_out, in_1[2]);
  not not_2 (not_2_out, in_1[0]);
  not not_3 (not_3_out, in_1[3]);
  not not_4 (not_4_out, in_1[1]);
  not not_5 (not_5_out, in_1[0]);
  not not_6 (not_6_out, in_1[1]);
  not not_7 (not_7_out, in_1[0]);
  not not_8 (not_8_out, in_1[3]);
  not not_9 (not_9_out, in_1[1]);
  not not_10 (not_10_out, in_1[2]);
  not not_11 (not_11_out, in_1[2]);
  not not_12 (not_12_out, in_1[0]);
  not not_13 (not_13_out, in_1[3]);
  not not_14 (not_14_out, in_1[2]);
  not not_15 (not_15_out, in_1[0]);
  not not_16 (not_16_out, in_1[1]);
  not not_17 (not_17_out, in_1[1]);
  not not_18 (not_18_out, in_1[2]);
  not not_19 (not_19_out, in_1[0]);
  not not_20 (not_20_out, in_1[0]);
  not not_21 (not_21_out, in_1[0]);
  not not_22 (not_22_out, in_1[3]);
  not not_23 (not_23_out, in_1[1]);
  not not_24 (not_24_out, in_1[0]);
  not not_25 (not_25_out, in_1[3]);
  not not_26 (not_26_out, in_1[0]);
  not not_27 (not_27_out, in_1[1]);
  not not_28 (not_28_out, in_1[2]);
  not not_29 (not_29_out, in_1[1]);
  not not_30 (not_30_out, in_1[0]);
  not not_31 (not_31_out, in_1[3]);
  not not_32 (not_32_out, in_1[2]);
  not not_33 (not_33_out, in_1[1]);
  not not_34 (not_34_out, in_1[0]);
  not not_35 (not_35_out, in_1[1]);
  and and_1 (and_1_out, not_1_out, not_2_out);
  and and_2 (and_2_out, not_3_out, in_1[1]);
  and and_3 (and_3_out, in_1[2], in_1[0]);
  and and_4 (and_4_out, in_1[3], not_4_out);
  and and_5 (and_5_out, in_1[3], not_5_out);
  not not_36 (not_36_out, in_1[2]);
  or or_1 (b, not_36_out, and_6_out, and_7_out);
  and and_6 (and_6_out, not_6_out, not_7_out);
  and and_7 (and_7_out, in_1[1], in_1[0]);
  and and_8 (and_8_out, not_8_out, not_9_out);
  and and_9 (and_9_out, in_1[2], in_1[1]);
  and and_10 (and_10_out, in_1[3], not_10_out);
  and and_11 (and_11_out, not_11_out, not_12_out);
  and and_12 (and_12_out, not_13_out, not_14_out, in_1[1]);
  and and_13 (and_13_out, in_1[1], not_15_out);
  and and_14 (and_14_out, in_1[2], not_16_out, in_1[0]);
  and and_15 (and_15_out, in_1[3], not_17_out);
  and and_16 (and_16_out, in_1[3], in_1[2]);
  and and_17 (and_17_out, not_18_out, not_19_out);
  or or_2 (e, and_17_out, and_18_out, and_19_out);
  and and_18 (and_18_out, in_1[1], not_20_out);
  and and_19 (and_19_out, in_1[3], not_21_out);
  and and_20 (and_20_out, not_22_out, not_23_out, not_24_out);
  and and_21 (and_21_out, not_25_out, in_1[2], not_26_out);
  and and_22 (and_22_out, in_1[2], not_27_out, in_1[0]);
  and and_23 (and_23_out, in_1[3], not_28_out, not_29_out);
  and and_24 (and_24_out, in_1[3], in_1[1], not_30_out);
  and and_25 (and_25_out, not_31_out, not_32_out, in_1[1]);
  and and_26 (and_26_out, in_1[2], not_33_out);
  and and_27 (and_27_out, in_1[2], not_34_out);
  and and_28 (and_28_out, in_1[3], not_35_out);
  and and_29 (and_29_out, in_1[3], in_1[2]);
  or or_3 (a, and_1_out, and_2_out, and_3_out, and_4_out, and_5_out);
  or or_4 (c, and_8_out, in_1[0], and_9_out, and_10_out);
  or or_5 (d, and_11_out, and_12_out, and_13_out, and_14_out, and_15_out, and_16_out);
  or or_6 (f, and_20_out, and_21_out, and_22_out, and_23_out, and_24_out);
  or or_7 (g, and_25_out, and_26_out, and_27_out, and_28_out, and_29_out);
endmodule

module _0_9_counter (
  input  Set,
  input  Clock,
  output [3:0] \output ,
  output reset
);

  wire n0_9_counter_logic_1_d0, n0_9_counter_logic_1_d1, n0_9_counter_logic_1_d2, n0_9_counter_logic_1_d3,
       or_1_out;

  _0_9_counter_logic u_0_9_counter_logic_1 (
    .Q3(\output [3]), .Q2(\output [2]), .Q1(\output [1]), .Q0(\output [0]), .D3(n0_9_counter_logic_1_d3),
    .D2(n0_9_counter_logic_1_d2), .D1(n0_9_counter_logic_1_d1), .D0(n0_9_counter_logic_1_d0), .Reset(reset));
  or or_1 (or_1_out, Set, Clock);
  D_Flip_Flop d_ff_1 (
    .clk(or_1_out), .D(n0_9_counter_logic_1_d3), .Q(\output [3]), .reset(reset));  // open: Qn, preset, en
  D_Flip_Flop d_ff_2 (
    .clk(or_1_out), .D(n0_9_counter_logic_1_d2), .Q(\output [2]), .reset(reset));  // open: Qn, preset, en
  D_Flip_Flop d_ff_3 (
    .clk(or_1_out), .D(n0_9_counter_logic_1_d1), .Q(\output [1]), .reset(reset));  // open: Qn, preset, en
  D_Flip_Flop d_ff_4 (
    .clk(or_1_out), .D(n0_9_counter_logic_1_d0), .Q(\output [0]), .reset(reset));  // open: Qn, preset, en
endmodule

module _0_9_counter_logic (
  input  Q3,
  input  Q2,
  input  Q1,
  input  Q0,
  output D3,
  output D2,
  output D1,
  output D0,
  output Reset
);

  wire and_1_out, and_2_out, and_3_out, and_4_out, and_5_out, and_6_out, and_7_out, and_8_out, and_9_out,
       not_1_out, not_2_out, not_3_out, not_4_out, not_5_out, not_6_out, not_7_out, not_8_out, not_9_out,
       not_11_out, not_12_out;

  not not_1 (not_1_out, Q3);
  not not_2 (not_2_out, Q2);
  not not_3 (not_3_out, Q1);
  not not_4 (not_4_out, Q0);
  not not_5 (not_5_out, Q2);
  and and_1 (and_1_out, not_5_out, Q1, Q0);
  and and_2 (and_2_out, Q2, not_6_out);
  not not_6 (not_6_out, Q1);
  and and_3 (and_3_out, Q2, not_7_out);
  not not_7 (not_7_out, Q0);
  not not_8 (not_8_out, Q1);
  and and_4 (and_4_out, not_8_out, Q0);
  and and_5 (and_5_out, Q1, not_9_out);
  not not_9 (not_9_out, Q0);
  not not_10 (D0, Q0);
  not not_11 (not_11_out, Q2);
  not not_12 (not_12_out, Q0);
  and and_6 (and_6_out, not_1_out, Q2, Q1, Q0);
  and and_7 (and_7_out, Q3, not_2_out);
  and and_8 (and_8_out, Q3, not_3_out);
  and and_9 (and_9_out, Q3, not_4_out);
  or or_1 (D2, and_1_out, and_2_out, and_3_out);
  or or_2 (D1, and_4_out, and_5_out);
  and and_10 (Reset, Q3, not_11_out, Q1, not_12_out);
  or or_3 (D3, and_6_out, and_7_out, and_8_out, and_9_out);
endmodule

module _0_5_Counter (
  input  Set,
  input  clock,
  output [3:0] \output ,
  output reset
);

  wire n0_5_counter_logic_1_d0, n0_5_counter_logic_1_d1, n0_5_counter_logic_1_d2, or_1_out;

  _0_5_Counter_Logic u_0_5_counter_logic_1 (
    .Q2(\output [2]), .Q1(\output [1]), .Q0(\output [0]), .D3(\output [3]), .D2(n0_5_counter_logic_1_d2),
    .D1(n0_5_counter_logic_1_d1), .D0(n0_5_counter_logic_1_d0), .Reset(reset));
  or or_1 (or_1_out, Set, clock);
  D_Flip_Flop d_ff_1 (
    .clk(or_1_out), .D(n0_5_counter_logic_1_d2), .Q(\output [2]), .reset(reset));  // open: Qn, preset, en
  D_Flip_Flop d_ff_2 (
    .clk(or_1_out), .D(n0_5_counter_logic_1_d1), .Q(\output [1]), .reset(reset));  // open: Qn, preset, en
  D_Flip_Flop d_ff_3 (
    .clk(or_1_out), .D(n0_5_counter_logic_1_d0), .Q(\output [0]), .reset(reset));  // open: Qn, preset, en
endmodule

module _0_5_Counter_Logic (
  input  Q2,
  input  Q1,
  input  Q0,
  output D3,
  output D2,
  output D1,
  output D0,
  output Reset
);

  wire and_1_out, and_2_out, and_3_out, and_4_out, and_5_out, not_1_out, not_2_out, not_3_out, not_4_out,
       not_5_out, not_7_out;

  not not_1 (not_1_out, Q2);
  not not_2 (not_2_out, Q1);
  not not_3 (not_3_out, Q0);
  not not_4 (not_4_out, Q1);
  not not_5 (not_5_out, Q0);
  not not_6 (D0, Q0);
  not not_7 (not_7_out, Q0);
  and and_1 (and_1_out, not_1_out, Q1, Q0);
  and and_2 (and_2_out, Q2, not_2_out);
  and and_3 (and_3_out, Q2, not_3_out);
  and and_4 (and_4_out, not_4_out, Q0);
  and and_5 (and_5_out, Q1, not_5_out);
  and and_6 (Reset, Q2, Q1, not_7_out);
  or or_1 (D2, and_1_out, and_2_out, and_3_out);
  or or_2 (D1, and_4_out, and_5_out);

  assign D3 = 1'b0;
endmodule

module _0_12_counter_Logic (
  input  Q3,
  input  Q2,
  input  Q1,
  input  Q0,
  output D3,
  output D2,
  output D1,
  output D0,
  output Reset
);

  wire and_1_out, and_2_out, and_3_out, and_4_out, and_5_out, and_6_out, and_7_out, and_8_out, and_9_out,
       not_1_out, not_2_out, not_3_out, not_4_out, not_5_out, not_6_out, not_7_out, not_8_out, not_9_out,
       not_11_out;

  not not_1 (not_1_out, Q3);
  not not_2 (not_2_out, Q2);
  not not_3 (not_3_out, Q1);
  not not_4 (not_4_out, Q0);
  not not_5 (not_5_out, Q2);
  and and_1 (and_1_out, not_5_out, Q1, Q0);
  and and_2 (and_2_out, Q2, not_6_out);
  not not_6 (not_6_out, Q1);
  and and_3 (and_3_out, Q2, not_7_out);
  not not_7 (not_7_out, Q0);
  not not_8 (not_8_out, Q1);
  and and_4 (and_4_out, not_8_out, Q0);
  and and_5 (and_5_out, Q1, not_9_out);
  not not_9 (not_9_out, Q0);
  not not_10 (D0, Q0);
  not not_11 (not_11_out, Q2);
  and and_6 (and_6_out, not_1_out, Q2, Q1, Q0);
  and and_7 (and_7_out, Q3, not_2_out);
  and and_8 (and_8_out, Q3, not_3_out);
  and and_9 (and_9_out, Q3, not_4_out);
  or or_1 (D2, and_1_out, and_2_out, and_3_out);
  or or_2 (D1, and_4_out, and_5_out);
  and and_10 (Reset, Q3, not_11_out, Q1, Q0);
  or or_3 (D3, and_6_out, and_7_out, and_8_out, and_9_out);
endmodule

module _0_12_counter (
  input  Set,
  input  clock,
  output [3:0] \output ,
  output reset
);

  wire and_1_out, n0_12_counter_logic_1_d0, n0_12_counter_logic_1_d1, n0_12_counter_logic_1_d2,
       n0_12_counter_logic_1_d3, n0_12_counter_logic_1_reset, or_1_out;

  _0_12_counter_Logic u_0_12_counter_logic_1 (
    .Q3(\output [3]), .Q2(\output [2]), .Q1(\output [1]), .Q0(\output [0]), .D3(n0_12_counter_logic_1_d3),
    .D2(n0_12_counter_logic_1_d2), .D1(n0_12_counter_logic_1_d1), .D0(n0_12_counter_logic_1_d0),
    .Reset(n0_12_counter_logic_1_reset));
  or or_1 (or_1_out, Set, clock);
  D_Flip_Flop d_ff_1 (
    .clk(or_1_out), .D(n0_12_counter_logic_1_d3), .Q(\output [3]), .reset(and_1_out));  // open: Qn, preset, en
  D_Flip_Flop d_ff_2 (
    .clk(or_1_out), .D(n0_12_counter_logic_1_d2), .Q(\output [2]), .reset(and_1_out));  // open: Qn, preset, en
  D_Flip_Flop d_ff_3 (
    .clk(or_1_out), .D(n0_12_counter_logic_1_d1), .Q(\output [1]), .reset(and_1_out));  // open: Qn, preset, en
  D_Flip_Flop d_ff_4 (
    .clk(or_1_out), .D(n0_12_counter_logic_1_d0), .Q(\output [0]), .preset(and_1_out));  // open: Qn, en, reset
  and and_1 (and_1_out, \output [3], \output [2], \output [0]);
  and and_2 (reset, n0_12_counter_logic_1_reset, clock);
endmodule

module H_decoder (
  input  [3:0] in_1,
  output out_2,
  output out_3,
  output out_4,
  output O0
);

  wire and_1_out, and_2_out, not_1_out, not_2_out, not_3_out;

  not not_1 (not_1_out, in_1[2]);
  not not_2 (not_2_out, in_1[1]);
  not not_3 (not_3_out, in_1[0]);
  and and_1 (and_1_out, in_1[3], not_1_out, in_1[1]);
  and and_2 (and_2_out, in_1[3], in_1[2], not_2_out, not_3_out);
  or or_1 (O0, and_1_out, and_2_out);

  assign out_2 = 1'b0;
  assign out_3 = 1'b0;
  assign out_4 = 1'b0;
endmodule

module Clock (
  input  A_P,
  input  s,
  input  S_2,
  input  m,
  input  M_2,
  input  H,
  output [6:0] H_2,
  output [6:0] h_3,
  output [3:0] M_3,
  output [3:0] m_4,
  output [3:0] S_3,
  output [3:0] s_4,
  output C_A_P
);

  wire and_1_out, and_2_out, and_3_out, and_4_out, and_5_out, Clock_out, n0_5_counter_1_reset,
       n0_5_counter_2_reset, n0_9_counter_1_reset, n0_9_counter_2_reset, n0_12_counter_1_reset;
  wire [3:0] h_decoder_1_o0, n0_12_counter_1_output;

  Clock_part Clock (.out(Clock_out));
  _7_segment_decoder u_7_segment_decoder_1 (
    .a(H_2[0]), .b(H_2[1]), .c(H_2[2]), .d(H_2[3]), .e(H_2[4]), .f(H_2[5]), .g(H_2[6]), .in_1(h_decoder_1_o0));
  H_decoder h_decoder_1 (
    .in_1(n0_12_counter_1_output), .out_2(h_decoder_1_o0[3]), .out_3(h_decoder_1_o0[2]),
    .out_4(h_decoder_1_o0[1]), .O0(h_decoder_1_o0[0]));
  and and_1 (and_1_out, n0_12_counter_1_reset, Clock_out);
  _0_9_counter u_0_9_counter_1 (.Clock(Clock_out), .\output (s_4), .reset(n0_9_counter_1_reset), .Set(s));
  A_P_indicator a_p_indicator_1 (
    .Clock(and_1_out), .Set(A_P), .out_5(C_A_P));  // open: out_3, out_4, out_6, out_7, out_8, out_9
  and and_2 (and_2_out, n0_9_counter_1_reset, Clock_out);
  _0_5_Counter u_0_5_counter_1 (.clock(and_2_out), .\output (S_3), .reset(n0_5_counter_1_reset), .Set(S_2));
  _7_segment_decoder u_7_segment_decoder_2 (
    .a(h_3[0]), .b(h_3[1]), .c(h_3[2]), .d(h_3[3]), .e(h_3[4]), .f(h_3[5]), .g(h_3[6]),
    .in_1(n0_12_counter_1_output));
  _0_9_counter u_0_9_counter_2 (.Clock(and_3_out), .\output (m_4), .reset(n0_9_counter_2_reset), .Set(m));
  and and_3 (and_3_out, n0_5_counter_1_reset, Clock_out);
  _0_5_Counter u_0_5_counter_2 (.clock(and_4_out), .\output (M_3), .reset(n0_5_counter_2_reset), .Set(M_2));
  and and_4 (and_4_out, n0_9_counter_2_reset, Clock_out);
  and and_5 (and_5_out, n0_5_counter_2_reset, Clock_out);
  _0_12_counter u_0_12_counter_1 (
    .Set(H), .clock(and_5_out), .\output (n0_12_counter_1_output), .reset(n0_12_counter_1_reset));
endmodule

module A_P_indicator (
  input  Clock,
  input  Set,
  output out_3,
  output out_4,
  output out_5,
  output out_6,
  output out_7,
  output out_8,
  output out_9
);

  wire d_ff_1_qn, or_1_out;

  or or_1 (or_1_out, Clock, Set);
  D_Flip_Flop d_ff_1 (.clk(or_1_out), .D(d_ff_1_qn), .Q(out_5), .Qn(d_ff_1_qn));  // open: preset, en, reset

  assign out_3 = 1'b1;
  assign out_4 = 1'b1;
  assign out_6 = 1'b0;
  assign out_7 = 1'b1;
  assign out_8 = 1'b1;
  assign out_9 = 1'b1;
endmodule
